// Logisim project FSM (3).circ as structural Verilog: 1 circuit, main circuit main
module main (
  input  pressed,
  input  [3:0] code,
  output calc,
  output next,
  output [1:0] op,
  output rst
);

  wire and_2_out, and_3_out, and_4_out, eq_out, nand_1_out, nnum_out, not_1_out, not_2_out, not_3_out,
       or_2_out, xor_1_out;
  wire [1:0] or_1_out, state_q;

  and and_1 (or_1_out[1], xor_1_out, eq_out);
  or or_1 (or_1_out[0], and_3_out, and_2_out);
  and and_2 (and_2_out, nand_1_out, and_4_out);
  and and_3 (and_3_out, next, not_2_out);
  and u_op (next, nnum_out, nand_1_out);
  and nnum (nnum_out, code[3], or_2_out);
  nand nand_1 (nand_1_out, code[3], code[2], code[1]);
  or or_2 (or_2_out, code[1], code[2]);
  Register #(.width(2)) state (.D(or_1_out), .Q(state_q), .clk(pressed));  // open: en, clr
  not not_1 (not_1_out, state_q[1]);
  and and_4 (and_4_out, not_1_out, state_q[0]);
  and eq (eq_out, code[3], code[2], code[1], not_3_out);
  xor xor_1 (xor_1_out, state_q[0], state_q[1]);
  and and_5 (calc, state_q[1], not_2_out);
  not not_2 (not_2_out, state_q[0]);
  not not_3 (not_3_out, code[0]);
  and u_rst (rst, code[0], code[1], code[2], code[3]);

  assign op = {code[2], code[0]};
endmodule
